# Fritzing sketch PCB (saved by Fritzing 0.9.3b)
perfboards: 2

parts:
  Part1 = Arduino Pro Mini v13
  S1 = Pushbutton [package="[THT]"]
  S2 = Pushbutton [package="[THT]"]
  U1 = TEMPERATURE-SENSOR [package=to-92]
  LED1 = LED - 5mm [color="Green (555nm)" package="5 mm [THT]"]
  LED2 = LED - 5mm [color="Red (633nm)" package="5 mm [THT]"]
  R4 = Resistor [tolerance=±5% resistance=220 package=THT]
  R5 = Resistor [tolerance=±5% resistance=220 package=THT]
  R1 = Rotary Potentiometer (Small) [maximum_resistance=100kΩ package=THT]
  R10 = Resistor [tolerance=±5% resistance=220 package=THT]
  C7 = Ceramic Capacitor [capacitance=100nF package="100 mil [THT, multilayer]"]
  R11 = Rotary Potentiometer (Small) [maximum_resistance=100kΩ package=THT]
  IC4 = MICROCONTROLLER [package=dil28-3-simon]
  S5 = Pushbutton [package="[THT]"]
  C8 = Ceramic Capacitor [capacitance=100nF package="100 mil [THT, multilayer]"]
  XTAL4 = Crystal [frequency="16 Mhz" package=THT]
  LED5 = LED - 5mm [color="Red (633nm)" package="5 mm [THT]"]
  J2 = male pin header, 7 pins [form="♂ (male)"]
  R12 = Resistor [tolerance=±5% resistance=220 package=THT]

nets:
  N1: Part1.A3, S2.Pin_3, S2.Pin_4
  N2: Part1.A2, U1.ADJ
  N3: Part1.A1, S1.Pin_3, S1.Pin_4
  N4: Part1.A0, R1.wiper
  N5: Part1.D10_PWM/SS, LED1.anode
  N6: Part1.D9_PWM, LED2.anode
  N7: S1.Pin_1, S1.Pin_2
  N8: S2.Pin_1, S2.Pin_2
  N9: LED1.cathode, R5.Pin_1
  N10: LED2.cathode, R4.Pin_1
  N11: R10.Pin_0, R11.leg1, IC4.VCC, IC4.AVCC
  N12: R10.Pin_1, IC4.PC6(_RESET)
  N13: C7.0, IC4.PB6(XTAL1_TOSC1), XTAL4.pin_1
  N14: C7.1, IC4.GND, IC4.AGND, S5.Pin_3, S5.Pin_4, C8.0, J2.pin1, J2.pin6
  N15: R11.wiper, IC4.PC0(ADC0)
  N16: R11.leg2, R12.Pin_0
  N17: IC4.PD2(INT0), S5.Pin_1, S5.Pin_2
  N18: IC4.PD3(INT1), J2.pin3
  N19: IC4.PD4(XCK_T0), J2.pin2
  N20: IC4.PB7(XTAL2_TOSC2), C8.1, XTAL4.pin_0
  N21: IC4.PB2(SS_OC1B), LED5.anode
  N22: IC4.PC2(ADC2), J2.pin7
  N23: LED5.cathode, R12.Pin_1
